# Fritzing sketch Rain-Monitor (saved by Fritzing 0.9.3b)
circuit board: 6.52541cm x 5.62539cm
breadboards: 1

parts:
  LCD = Adafruit Negative RGB 2x16 LCD
  POT1 = Breadboard Trimpot
  J1 = Cobbler Plus Cable
  Raspberry_Pi_1 = Raspberry Pi 3 [part_number=RPI-3-V1.2]  # not connected
  R1 = Resistor [tolerance=±5% resistance=1k package=THT]
  D1 = Zener Diode [part_number=1N4732A breakdown_voltage=3.6V package="300 mil [THT]"]
  Q1 = NPN-Transistor [package="TO92 [THT]"]
  J1_2 = Screw terminal - 2 pins [package=THT]
  LED(R) = LED - 3mm [color="Red (633nm)" package="3 mm [THT]"]
  LED(Y) = LED - 3mm [color="Yellow (595nm)" package="3 mm [THT]"]
  LED(G) = LED - 3mm [color="Green (565nm)" package="3 mm [THT]"]
  Relay = songle relay

nets:
  N1: LCD.no_name_yet#0, LCD.no_name_yet#4, POT1.PIN1, J1.GND#8, J1.GND#24, J1.GND#38, Q1.E, LED(R).cathode, LED(Y).cathode, LED(G).cathode
  N2: LCD.no_name_yet#1, LCD.no_name_yet#14, POT1.PIN3, J1.5.0V#1, D1.cathode, Relay.GND
  N3: LCD.no_name_yet#2, POT1.PIN2
  N4: LCD.no_name_yet#3, J1.#27
  N5: LCD.no_name_yet#5, J1.#22
  N6: LCD.no_name_yet#10, J1.#5
  N7: LCD.no_name_yet#11, J1.#6
  N8: LCD.no_name_yet#12, J1.#13
  N9: LCD.no_name_yet#13, J1.#19
  N10: LCD.no_name_yet#15, J1.#4
  N11: LCD.no_name_yet#16, J1.#17
  N12: LCD.no_name_yet#17, J1.#26
  N13: J1.#12, LED(G).anode
  N14: J1.#16, LED(Y).anode
  N15: J1.#20, LED(R).anode
  N16: J1.#21, R1.Pin_1
  N17: R1.Pin_0, Q1.B
  N18: D1.anode, Q1.C, Relay.VCC
  N19: J1_2.pin1, Relay.NO
  N20: J1_2.pin2, Relay.COMMON

notes:
  1
  18
  k5map@arrl.net
  Rain Monitor v4

custom parts:
  Adafruit Negative RGB 2x16 LCD: Adafruit Negative 2x16 LCD Display with RGB Backlight
  Cobbler Plus Cable: The Cobbler Plus is an add on prototyping board from Adafruit specifically designed for the Raspberry Pi B+ that can break out all those tasty power, GPIO, I2C and SPI pins from the 40-pin header onto a solderless breadboard. This set will make "cobbling together" prototypes with the Pi super easy. The Cobbler Plus can plug into any solderless breadboard.
